// Logisim project CPU.circ as structural Verilog: 2 circuits, main circuit main
module main (
);

  wire alu_1_f_out, and_1_out, and_2_out, CLK, CLK_RAW, COMMIT_ALU, d_ff_1_q, d_ff_1_qn, FAULT, FAULTED,
       FLAG_BUS, HALT, HALTED, INSN_END, JMP, LOAD_A, LOAD_ALU, LOAD_B, LOAD_FLAG, LOAD_FLAG_INT,
       LOAD_FLAG_INV, LOAD_PROG, not_1_out, not_2_out, PROG_NEXT, register_6_q, RESET, STORE_A, STORE_B,
       STORE_DISPLAY, STORE_FLAG, STORE_INSN;
  wire [3:0] ALU_OP;
  wire [7:0] alu_1_out, bit_extender_1_out, BUS, counter_1_q, DISPLAY, INSN, PROG_ADDR, pull_resistor_3_node,
       REG_A, REG_B, register_5_q, rom_1_data;
  wire [31:17] rom_2_data;

  not not_1 (not_1_out, HALTED);
  assign CLK = not_1_out ? CLK_RAW : 1'bz;  // Controlled_Buffer controlled_buffer_1
  Pull_Resistor pull_resistor_1 (.node(CLK));
  Clock clock_1 (.out(CLK_RAW));
  Button button_1 (.out(RESET));
  // Probe on BUS
  // Probe on DISPLAY
  // Probe on DISPLAY
  Pull_Resistor pull_resistor_2 (.node(DISPLAY));
  // Probe on DISPLAY
  S_R_Flip_Flop s_r_ff_1 (.Q(HALTED), .preset(HALT), .reset(RESET));  // open: S, clk, R, Qn, en
  LED led_1 (.in(CLK));
  LED led_2 (.in(CLK));
  Pull_Resistor pull_resistor_3 (.node(pull_resistor_3_node));
  not not_2 (not_2_out, INSN_END);
  LED led_3 (.in(and_2_out));
  LED led_4 (.in(and_1_out));
  LED led_5 (.in(and_2_out));
  Register register_1 (.D(BUS), .en(STORE_INSN), .Q(INSN), .clk(CLK), .clr(RESET));
  Counter counter_1 (
    .load(INSN_END), .D(pull_resistor_3_node), .count(not_2_out), .Q(counter_1_q), .clk(CLK));  // open: carry, clr
  LED led_6 (.in(and_2_out));
  and and_1 (and_1_out, ~CLK_RAW, FAULTED);  // AND_Gate
  LED led_7 (.in(and_1_out));
  LED led_8 (.in(and_1_out));
  LED led_9 (.in(and_1_out));
  LED led_10 (.in(and_1_out));
  and and_2 (and_2_out, FAULTED, CLK_RAW);
  LED led_11 (.in(and_2_out));
  Register register_2 (.D(BUS), .en(STORE_DISPLAY), .Q(DISPLAY), .clk(CLK), .clr(RESET));
  Counter counter_2 (.load(JMP), .D(BUS), .count(PROG_NEXT), .Q(PROG_ADDR), .clk(CLK), .clr(RESET));  // open: carry
  // Probe on {INSN, counter_1_q}
  Pull_Resistor pull_resistor_4 (.node({INSN, counter_1_q}));
  S_R_Flip_Flop s_r_ff_2 (.Q(FAULTED), .preset(FAULT), .reset(RESET));  // open: S, clk, R, Qn, en
  assign BUS = LOAD_PROG ? rom_1_data : 8'bz;  // Controlled_Buffer controlled_buffer_2
  ROM rom_1 (.addr(PROG_ADDR), .data(rom_1_data));  // open: sel
  Pull_Resistor pull_resistor_5 (.node(LOAD_PROG));
  ROM #(.addrWidth(16), .dataWidth(32)) rom_2 (
    .addr({INSN, counter_1_q}),
    .data({rom_2_data, ALU_OP, COMMIT_ALU, STORE_DISPLAY, STORE_INSN, STORE_B, STORE_A, LOAD_ALU, LOAD_B, LOAD_A, FAULT, HALT, LOAD_PROG, PROG_NEXT, INSN_END}));  // open: sel
  Pull_Resistor pull_resistor_6 (.node(FLAG_BUS));
  Pull_Resistor pull_resistor_7 (.node(STORE_FLAG));
  Pull_Resistor pull_resistor_8 (.node(LOAD_FLAG_INV));
  Pull_Resistor pull_resistor_9 (.node(LOAD_FLAG));
  Pull_Resistor pull_resistor_10 (.node(LOAD_FLAG_INT));
  ALU alu_1 (.OP(ALU_OP), .A(REG_A), .B(REG_B), .OUT(alu_1_out), .F_OUT(alu_1_f_out));
  assign BUS = LOAD_A ? REG_A : 8'bz;  // Controlled_Buffer controlled_buffer_3
  Register register_3 (.D(BUS), .en(STORE_A), .Q(REG_A), .clk(CLK), .clr(RESET));
  Pull_Resistor pull_resistor_11 (.node(LOAD_A));
  assign BUS = LOAD_B ? REG_B : 8'bz;  // Controlled_Buffer controlled_buffer_4
  Register register_4 (.D(BUS), .en(STORE_B), .Q(REG_B), .clk(CLK), .clr(RESET));
  Pull_Resistor pull_resistor_12 (.node(LOAD_B));
  assign FLAG_BUS = LOAD_FLAG ? d_ff_1_q : 1'bz;  // Controlled_Buffer controlled_buffer_5
  D_Flip_Flop d_ff_1 (
    .clk(FLAG_BUS), .D(CLK), .Q(d_ff_1_q), .Qn(d_ff_1_qn), .en(STORE_FLAG), .reset(RESET));  // open: preset
  assign FLAG_BUS = LOAD_FLAG_INV ? d_ff_1_qn : 1'bz;  // Controlled_Buffer controlled_buffer_6
  Pull_Resistor pull_resistor_13 (.node(LOAD_ALU));
  Register register_5 (.D(alu_1_out), .en(COMMIT_ALU), .Q(register_5_q), .clk(CLK), .clr(RESET));
  Register #(.width(1)) register_6 (.D(alu_1_f_out), .en(COMMIT_ALU), .Q(register_6_q), .clk(CLK), .clr(RESET));
  LED led_12 (.in(CLK));
  assign bit_extender_1_out = {{7{1'b0}}, FLAG_BUS};  // Bit_Extender bit_extender_1
  assign BUS = LOAD_ALU ? register_5_q : 8'bz;  // Controlled_Buffer controlled_buffer_7
  assign FLAG_BUS = LOAD_ALU ? register_6_q : 1'bz;  // Controlled_Buffer controlled_buffer_8
  LED led_13 (.in(CLK));
  assign BUS = LOAD_FLAG_INT ? bit_extender_1_out : 8'bz;  // Controlled_Buffer controlled_buffer_9

  // Notes on the sheet:
  //   Halt
  //   Display
  //   Instruction register
  //   Fault
  //   Program Counter
  //   Program ROM
  //   Control Unit ROM
  //   contents of rom_1 (hex, n*v repeats v):
  //   13 6 23 7 42 32 2
  //   contents of rom_2 (hex, n*v repeats v):
  //   405 255*0 2 405 254*0 8 2 405 3581*0 120 2 405 253*0 140 2 405 253*0 180 2 405 253*0 2 104 2 405
  //   252*0 118 2 405 253*0 118 2 405 253*0 118 2 405 253*0 118 2 405 253*0 118 2 405 253*0 118 2 405
  //   253*0 118 2 405 253*0 118 2 405 253*0 118 2 405 253*0 118 2 405 253*0 118 2 405 253*0 118 2 405
  //   253*0 220 2 405 253*0 240 2 405 253*0 280 2 405 253*0 2 204 2 405 252*0 218 2 405 253*0 218 2 405
  //   253*0 218 2 405 253*0 218 2 405 253*0 218 2 405 253*0 218 2 405 253*0 218 2 405 253*0 218 2 405
  //   253*0 218 2 405 253*0 218 2 405 253*0 218 2 405 253*0 218 2 405 253*0 820 2 405 253*0 840 2 405
  //   253*0 880 2 405 253*0 2 804 2 405 252*0 818 2 405 253*0 818 2 405 253*0 818 2 405 253*0 818 2 405
  //   253*0 818 2 405 253*0 818 2 405 253*0 818 2 405 253*0 818 2 405 253*0 818 2 405 253*0 818 2 405
  //   253*0 818 2 405 253*0 818 2 405 509*0 3000 2 405 253*0 5000 2 405 253*0 7000 2 405 253*0 9000 2 405
  //   253*0 b000 2 405 253*0 d000 2 405 253*0 f000 2 405 253*0 11000 2 405 253*0 13000 2 405 253*0 15000 2
  //   405 253*0 17000 2 405 253*0 19000 2 405 253*0 1b000 2 405 253*0 1d000 2 405 253*0 1f000 2 405 205
  //   Registers
  //   Flags Register
  //   ALU
endmodule

module ALU (
  input  [3:0] OP,
  input  [7:0] A,
  input  [7:0] B,
  output [7:0] OUT,
  output F_OUT
);

  wire comparator_1_eq, comparator_1_gt, comparator_1_lt, decoder_1_out0, decoder_1_out1, decoder_1_out2,
       decoder_1_out3, decoder_1_out4, decoder_1_out5, decoder_1_out6, decoder_1_out7, decoder_1_out8,
       decoder_1_out9, decoder_1_out10, decoder_1_out11, decoder_1_out12, decoder_1_out13, decoder_1_out14,
       decoder_1_out15, pull_resistor_5_node, pull_resistor_6_node;
  wire [1:0] pull_resistor_3_node, pull_resistor_4_node;
  wire [2:0] bitselector_1_out, bitselector_2_out;
  wire [3:0] bitadder_1_out;
  wire [7:0] adder_1_out, and_1_out, bit_extender_1_out, divider_1_out, multiplier_1_out, negator_1_out,
       not_1_out, or_1_out, pull_resistor_7_node, pull_resistor_8_node, shifter_1_out, shifter_2_out,
       subtractor_1_out, xor_1_out;

  Pull_Resistor pull_resistor_1 (.node(A));
  Pull_Resistor pull_resistor_2 (.node(B));
  Pull_Resistor pull_resistor_3 (.node(pull_resistor_3_node));
  Pull_Resistor pull_resistor_4 (.node(pull_resistor_4_node));
  Pull_Resistor pull_resistor_5 (.node(pull_resistor_5_node));
  Pull_Resistor pull_resistor_6 (.node(pull_resistor_6_node));
  Pull_Resistor pull_resistor_7 (.node(pull_resistor_7_node));
  Pull_Resistor pull_resistor_8 (.node(pull_resistor_8_node));
  BitSelector #(.group(3)) bitselector_1 (.in(B), .out(bitselector_1_out), .sel(pull_resistor_3_node));
  BitSelector #(.group(3)) bitselector_2 (.in(B), .out(bitselector_2_out), .sel(pull_resistor_4_node));
  Adder adder_1 (.a(A), .b(B), .out(adder_1_out), .cin(pull_resistor_5_node));  // open: cout
  Subtractor subtractor_1 (.a(A), .b(B), .out(subtractor_1_out), .bin(pull_resistor_6_node));  // open: bout
  Multiplier multiplier_1 (.a(A), .b(B), .out(multiplier_1_out), .cin(pull_resistor_7_node));  // open: cout
  Divider divider_1 (.a(A), .b(B), .out(divider_1_out), .upper(pull_resistor_8_node));  // open: rem
  Negator negator_1 (.in(A), .out(negator_1_out));
  Shifter shifter_1 (.in(A), .\dist (bitselector_1_out), .out(shifter_1_out));
  Shifter #(.shift("lr")) shifter_2 (.in(A), .\dist (bitselector_2_out), .out(shifter_2_out));
  BitAdder bitadder_1 (.in0(A), .out(bitadder_1_out));
  Comparator comparator_1 (.a(A), .b(B), .gt(comparator_1_gt), .eq(comparator_1_eq), .lt(comparator_1_lt));
  assign not_1_out = ~A;  // NOT_Gate not_1, 8 bits wide
  assign and_1_out = A & B;  // AND_Gate and_1, 8 bits wide
  assign or_1_out = A | B;  // OR_Gate or_1, 8 bits wide
  assign xor_1_out = A ^ B;  // XOR_Gate xor_1, 8 bits wide
  Decoder #(.select(4)) decoder_1 (
    .out0(decoder_1_out0), .out1(decoder_1_out1), .out2(decoder_1_out2), .out3(decoder_1_out3),
    .out4(decoder_1_out4), .out5(decoder_1_out5), .out6(decoder_1_out6), .out7(decoder_1_out7),
    .out8(decoder_1_out8), .out9(decoder_1_out9), .out10(decoder_1_out10), .out11(decoder_1_out11),
    .out12(decoder_1_out12), .out13(decoder_1_out13), .out14(decoder_1_out14), .out15(decoder_1_out15),
    .sel(OP));  // open: en
  Pull_Resistor pull_resistor_9 (.node(OP));
  assign OUT = decoder_1_out0 ? adder_1_out : 8'bz;  // Controlled_Buffer controlled_buffer_1
  assign OUT = decoder_1_out1 ? subtractor_1_out : 8'bz;  // Controlled_Buffer controlled_buffer_2
  assign OUT = decoder_1_out2 ? multiplier_1_out : 8'bz;  // Controlled_Buffer controlled_buffer_3
  assign OUT = decoder_1_out3 ? divider_1_out : 8'bz;  // Controlled_Buffer controlled_buffer_4
  assign OUT = decoder_1_out4 ? negator_1_out : 8'bz;  // Controlled_Buffer controlled_buffer_5
  assign OUT = decoder_1_out5 ? shifter_1_out : 8'bz;  // Controlled_Buffer controlled_buffer_6
  assign OUT = decoder_1_out6 ? shifter_2_out : 8'bz;  // Controlled_Buffer controlled_buffer_7
  assign OUT = decoder_1_out7 ? bit_extender_1_out : 8'bz;  // Controlled_Buffer controlled_buffer_8
  assign bit_extender_1_out = {{4{1'b0}}, bitadder_1_out};  // Bit_Extender bit_extender_1
  assign F_OUT = decoder_1_out8 ? comparator_1_eq : 1'bz;  // Controlled_Buffer controlled_buffer_9
  assign F_OUT = decoder_1_out9 ? ~comparator_1_eq : 1'bz;  // Controlled_Inverter controlled_inverter_1
  assign F_OUT = decoder_1_out10 ? comparator_1_lt : 1'bz;  // Controlled_Buffer controlled_buffer_10
  assign F_OUT = decoder_1_out11 ? comparator_1_gt : 1'bz;  // Controlled_Buffer controlled_buffer_11
  assign OUT = decoder_1_out12 ? not_1_out : 8'bz;  // Controlled_Buffer controlled_buffer_12
  assign OUT = decoder_1_out13 ? and_1_out : 8'bz;  // Controlled_Buffer controlled_buffer_13
  assign OUT = decoder_1_out14 ? or_1_out : 8'bz;  // Controlled_Buffer controlled_buffer_14
  assign OUT = decoder_1_out15 ? xor_1_out : 8'bz;  // Controlled_Buffer controlled_buffer_15
  Pull_Resistor pull_resistor_10 (.node(OUT));
  Pull_Resistor pull_resistor_11 (.node(F_OUT));

  // Notes on the sheet:
  //   0b0000 - ADD
  //   0b0001 - SUB
  //   0b0010 - MUL
  //   0b0011 - DIV
  //   0b0100 - NEG
  //   0b0101 - SHL
  //   0b0110 - SHR
  //   0b0111 - CNT
  //   0b1000 - CMPEQ
  //   0b1001 - CMPNEQ
  //   0b1010 - CMPLT
  //   0b1011 - CMPGT
  //   0b1100 - NOT
  //   0b1101 - AND
  //   0b1110 - OR
  //   0b1111 - XOR
endmodule
