// Logisim project CPU2.circ as structural Verilog: 2 circuits, main circuit main
module main (
  output [31:0] out_1
);

  wire AluA_EnableSigned, AluA_RightValue_PinZero, AluA_WriteOutput, and_1_out, and_2_out, big_rom_1_p1,
       big_rom_1_p2, buffer_1_out, CLK, clock_1_out, comparator_1_eq, DoJump, DoJump_IfNonZero,
       DoJump_IfZero, HALT, JumpDest_UseReg, JumpDest_UseRom, LoadInsn_FromRom, MovByte_Write,
       MovRam_AddrReg_READ, MovRam_UseConstAddr, MovRam_WriteFromRam, MovRam_WriteToRam, MovRom_Write,
       MovTiny_Write, not_1_out, or_1_out, ProgramCounter_Advance, pull_resistor_2_node, pull_resistor_3_node;
  wire [1:0] AluA_LeftReg_PayloadField, AluA_Op_PayloadField, AluA_OutReg_PayloadField,
       AluA_RightReg_PayloadField, JumpDest_Reg_PayloadField, MovRam_AddrReg_PayloadField,
       MovRam_DataReg_PayloadField, MovRom_Reg_PayloadField;
  wire [4:0] AluA_LeftReg, AluA_Op, AluA_OutReg, AluA_RightReg, JumpDest_Reg, MovRam_AddrReg, MovRam_DataReg,
       MovRom_Reg, MovTinyA_Reg, MovTinyB_Reg;
  wire [7:0] counter_2_q, pull_resistor_4_node;
  wire [11:0] IR_q;
  wire [14:0] RamAddr;
  wire [15:0] counter_1_q;
  wire [19:0] InsnPayload;
  wire [31:0] AluA_LeftValue, AluA_Result, AluA_RightValue, controlled_buffer_2_out, JumpDest, MovByte_Value,
       MovTinyA_Value, MovTinyB_Value, pull_resistor_1_node, RamValue, RomValue;

  Pull_Resistor pull_resistor_1 (.node(pull_resistor_1_node));
  Clock clock_1 (.out(clock_1_out));
  Comparator #(.width(32), .mode("unsigned")) comparator_1 (
    .a(pull_resistor_1_node), .b(AluA_Result), .eq(comparator_1_eq));  // open: gt, lt
  xor xor_1 (CLK, clock_1_out, buffer_1_out);
  buf buffer_1 (buffer_1_out, clock_1_out);
  and and_1 (and_1_out, DoJump_IfZero, comparator_1_eq);
  and and_2 (and_2_out, ~comparator_1_eq, DoJump_IfNonZero);  // AND_Gate
  or or_1 (or_1_out, and_1_out, and_2_out, DoJump);
  ROM #(.addrWidth(16), .dataWidth(32)) PROG (.addr(counter_1_q), .data(RomValue));
  Counter #(.width(16), .max('hffff)) counter_1 (
    .load(or_1_out), .up(pull_resistor_2_node), .count(ProgramCounter_Advance), .clk(CLK), .Q(counter_1_q));  // open: clr, D, carry
  Pull_Resistor #(.pull(1)) pull_resistor_2 (.node(pull_resistor_2_node));
  // Mini_Bit_Selector #(.in_width(32), .out_width(16)) mini_bit_selector_1: pin names not known; wires that end beside it: JumpDest
  Counter counter_2 (
    .load(LoadInsn_FromRom), .up(pull_resistor_3_node), .count(pull_resistor_3_node), .clk(CLK),
    .D(pull_resistor_4_node), .Q(counter_2_q));  // open: clr, carry
  Pull_Resistor #(.pull(1)) pull_resistor_3 (.node(pull_resistor_3_node));
  Pull_Resistor pull_resistor_4 (.node(pull_resistor_4_node));
  Register #(.width(32)) IR (.D(RomValue), .en(LoadInsn_FromRom), .clk(CLK), .Q({IR_q, InsnPayload}));  // open: clr
  assign JumpDest = JumpDest_UseRom ? RomValue : 32'bz;  // Controlled_Buffer controlled_buffer_1
  RAM #(.addrWidth(15), .dataWidth(32)) ram_1 (
    .addr(RamAddr), .we(MovRam_WriteToRam), .oe(MovRam_WriteFromRam), .clk(CLK), .data(RamValue));
  // Big_ROM #(.addressWidth(20), .valueWidth(64)) big_rom_1: pin names not known; wires that end beside it: big_rom_1_p1, big_rom_1_p2
  // Splitter #(.fanout(32), .incoming(32), .appear("right"), .spacing("double")) splitter_1: pin names not known; wires that end beside it: big_rom_1_p1, HALT, LoadInsn_FromRom
  // Splitter #(.appear("center"), .spacing("double")) splitter_2: pin names not known; wires that end beside it: ProgramCounter_Advance, MovRom_Write, MovRom_Reg_PayloadField
  // Splitter #(.appear("center"), .spacing("double")) splitter_3: pin names not known; wires that end beside it: AluA_LeftReg_PayloadField
  // Splitter #(.appear("center"), .spacing("double")) splitter_4: pin names not known; wires that end beside it: AluA_RightReg_PayloadField
  // Splitter #(.appear("center"), .spacing("double")) splitter_5: pin names not known; wires that end beside it: AluA_OutReg_PayloadField
  // Splitter #(.appear("center"), .spacing("double")) splitter_6: pin names not known; wires that end beside it: AluA_EnableSigned, AluA_WriteOutput, DoJump, AluA_Op_PayloadField
  // Splitter #(.appear("center"), .spacing("double")) splitter_7: pin names not known; wires that end beside it: JumpDest_UseRom, JumpDest_UseReg, MovByte_Write, MovTiny_Write, DoJump_IfNonZero, DoJump_IfZero, AluA_RightValue_PinZero, JumpDest_Reg_PayloadField
  // Splitter #(.appear("center"), .spacing("double")) splitter_8: pin names not known; wires that end beside it: MovRam_WriteToRam, MovRam_WriteFromRam, MovRam_UseConstAddr, MovRam_AddrReg_READ, MovRam_DataReg_PayloadField
  // Splitter #(.fanout(32), .incoming(32), .appear("right"), .spacing("double")) splitter_9: pin names not known; wires that end beside it: big_rom_1_p2
  // Splitter #(.appear("center"), .spacing("double")) splitter_10: pin names not known; wires that end beside it: MovRam_AddrReg_PayloadField
  not not_1 (not_1_out, AluA_RightValue_PinZero);
  assign controlled_buffer_2_out = not_1_out ? AluA_RightValue : 32'bz;  // Controlled_Buffer controlled_buffer_2
  Pull_Resistor pull_resistor_5 (.node(controlled_buffer_2_out));
  // ALU #(.width(32)) alu_1: pin names not known; wires that end beside it: AluA_EnableSigned, AluA_Op, AluA_LeftValue, controlled_buffer_2_out, AluA_Result
  Multiplexer #(.select(2), .width(5), .enable("false")) multiplexer_1 (
    .in0(InsnPayload[4:0]), .in1(InsnPayload[9:5]), .in2(InsnPayload[14:10]), .in3(InsnPayload[19:15]),
    .out(MovRom_Reg), .sel(MovRom_Reg_PayloadField));
  Multiplexer #(.select(2), .width(5), .enable("false")) multiplexer_2 (
    .in0(InsnPayload[4:0]), .in1(InsnPayload[9:5]), .in2(InsnPayload[14:10]), .in3(InsnPayload[19:15]),
    .out(AluA_LeftReg), .sel(AluA_LeftReg_PayloadField));
  Multiplexer #(.select(2), .width(5), .enable("false")) multiplexer_3 (
    .in0(InsnPayload[4:0]), .in1(InsnPayload[9:5]), .in2(InsnPayload[14:10]), .in3(InsnPayload[19:15]),
    .out(AluA_RightReg), .sel(AluA_RightReg_PayloadField));
  Multiplexer #(.select(2), .width(5), .enable("false")) multiplexer_4 (
    .in0(InsnPayload[4:0]), .in1(InsnPayload[9:5]), .in2(InsnPayload[14:10]), .in3(InsnPayload[19:15]),
    .out(AluA_OutReg), .sel(AluA_OutReg_PayloadField));
  Multiplexer #(.select(2), .width(5), .enable("false")) multiplexer_5 (
    .in0(InsnPayload[4:0]), .in1(InsnPayload[9:5]), .in2(InsnPayload[14:10]), .in3(InsnPayload[19:15]),
    .out(AluA_Op), .sel(AluA_Op_PayloadField));
  Multiplexer #(.select(2), .width(5), .enable("false")) multiplexer_6 (
    .in0(InsnPayload[4:0]), .in1(InsnPayload[9:5]), .in2(InsnPayload[14:10]), .in3(InsnPayload[19:15]),
    .out(JumpDest_Reg), .sel(JumpDest_Reg_PayloadField));
  // Mini_Bit_Extender #(.out_width(32)) mini_bit_extender_1: pin names not known; wires that end beside it: InsnPayload[7:0], MovByte_Value
  // Mini_Bit_Extender #(.in_width(5), .out_width(32)) mini_bit_extender_2: pin names not known; wires that end beside it: MovTinyB_Value
  // Mini_Bit_Extender #(.in_width(5), .out_width(32)) mini_bit_extender_3: pin names not known; wires that end beside it: MovTinyA_Value
  // Splitter #(.fanout(4), .incoming(20), .appear("center"), .spacing("double"), .bit1(0), .bit2(0), .bit3(0), .bit4(0), .bit5(1), .bit6(1), .bit7(1), .bit8(1), .bit9(1), .bit10(2), .bit11(2), .bit12(2), .bit13(2), .bit14(2), .bit15(3), .bit16(3), .bit17(3), .bit18(3), .bit19(3)) splitter_11: pin names not known; wires that end beside it: InsnPayload, MovTinyB_Reg, MovTinyA_Reg
  // Mini_Bit_Selector #(.in_width(20), .out_width(15)) mini_bit_selector_2: pin names not known; wires that end beside it: InsnPayload
  Controlled_Buffer #(.width(15)) controlled_buffer_3 (.out(RamAddr), .en(MovRam_UseConstAddr));  // open: in
  Multiplexer #(.select(2), .width(5), .enable("false")) multiplexer_7 (
    .in0(InsnPayload[4:0]), .in1(InsnPayload[9:5]), .in2(InsnPayload[14:10]), .in3(InsnPayload[19:15]),
    .out(MovRam_AddrReg), .sel(MovRam_AddrReg_PayloadField));
  Multiplexer #(.select(2), .width(5), .enable("false")) multiplexer_8 (
    .in0(InsnPayload[4:0]), .in1(InsnPayload[9:5]), .in2(InsnPayload[14:10]), .in3(InsnPayload[19:15]),
    .out(MovRam_DataReg), .sel(MovRam_DataReg_PayloadField));
  // Register_Bank #(.width(32), .registerCount(32), .portCount(32)) register_bank_1: pin names not known; wires that end beside it: JumpDest_Reg, AluA_OutReg, AluA_RightReg, AluA_LeftReg, MovRom_Reg, CLK, MovByte_Value, AluA_WriteOutput, AluA_Result, MovRom_Write, RomValue, out_1, AluA_RightValue, AluA_LeftValue
  // Mini_Bit_Selector #(.in_width(32), .out_width(15)) mini_bit_selector_3: pin names not known; wires that end beside it: MovRam_AddrReg, MovRam_DataReg, MovTinyB_Reg, MovTinyA_Reg, InsnPayload[19:15], MovRam_WriteFromRam, RamValue, MovTiny_Write, MovTinyB_Value, MovTiny_Write, MovTinyA_Value, MovRam_AddrReg_READ, MovRam_WriteToRam, RamValue, JumpDest_UseReg, JumpDest, RamAddr

  // Other names for the same wires on the sheet: MovByte_Reg[4:0] = InsnPayload[19:15]

  // Notes on the sheet:
  //   contents of PROG (hex, n*v repeats v):
  //   200001 355022 400280 208001 400681 420023 790c80 a 600000 4 790020 e 600000 2 400082 600000 2
endmodule

module viewer (
);

  wire [31:0] main_1_out_1;

  main main_1 (.out_1(main_1_out_1));
  // Probe on main_1_out_1
endmodule
